# Fritzing sketch rock_paper_scissors (saved by Fritzing 0.9.0b)
breadboards: 1

parts:
  S1 = Pushbutton [package="[THT]"]
  S2 = Pushbutton [package="[THT]"]
  S3 = Pushbutton [package="[THT]"]
  S4 = Pushbutton [package="[THT]"]
  Arduino1 = Arduino Uno (Rev3)

nets:
  N1: S1.Pin_1, S1.Pin_2, Arduino1.D2
  N2: S1.Pin_3, S1.Pin_4, S2.Pin_3, S2.Pin_4, S3.Pin_3, S3.Pin_4, S4.Pin_3, S4.Pin_4, Arduino1.GND
  N3: S2.Pin_1, S2.Pin_2
  N4: S3.Pin_1, S3.Pin_2, Arduino1.D4
  N5: S4.Pin_1, S4.Pin_2
